// Logisim project control-logic.circ as structural Verilog: 1 circuit, main circuit control_logic
module control_logic (
  input  [31:0] Instruction,
  input  BrEq,
  input  BrLt,
  output PCSel,
  output RegWEn,
  output [2:0] ImmSel,
  output BrUn,
  output ASel,
  output BSel,
  output [3:0] ALUSel,
  output MemRW,
  output [1:0] WBSel
);

  wire comparator_1_eq, comparator_2_eq, comparator_3_eq, comparator_4_eq, comparator_5_eq, comparator_6_eq,
       comparator_7_eq, comparator_8_eq, comparator_9_eq, comparator_10_eq, comparator_11_eq,
       comparator_12_eq, comparator_13_eq, comparator_14_eq, comparator_15_eq, comparator_16_eq,
       comparator_17_eq, comparator_18_eq, comparator_19_eq, is_addi, is_andi, is_ori, is_slli, is_slti,
       is_srai, is_srli, is_xori;
  wire [5:0] input_ROM;
  wire [15:0] rom_1_data;

  Comparator #(.width(5)) comparator_1 (.a(Instruction[6:2]), .b(5'b00100), .eq(comparator_1_eq));  // open: gt, lt
  Comparator #(.width(3)) comparator_2 (.a(Instruction[14:12]), .b(3'b000), .eq(comparator_2_eq));  // open: gt, lt
  Comparator #(.width(5)) comparator_3 (.a(Instruction[6:2]), .b(5'b00100), .eq(comparator_3_eq));  // open: gt, lt
  Comparator #(.width(3)) comparator_4 (.a(Instruction[14:12]), .b(3'b111), .eq(comparator_4_eq));  // open: gt, lt
  Comparator #(.width(5)) comparator_5 (.a(Instruction[6:2]), .b(5'b00100), .eq(comparator_5_eq));  // open: gt, lt
  Comparator #(.width(3)) comparator_6 (.a(Instruction[14:12]), .b(3'b110), .eq(comparator_6_eq));  // open: gt, lt
  Comparator #(.width(5)) comparator_7 (.a(Instruction[6:2]), .b(5'b00100), .eq(comparator_7_eq));  // open: gt, lt
  Comparator #(.width(3)) comparator_8 (.a(Instruction[14:12]), .b(3'b100), .eq(comparator_8_eq));  // open: gt, lt
  Comparator #(.width(5)) comparator_9 (.a(Instruction[6:2]), .b(5'b00100), .eq(comparator_9_eq));  // open: gt, lt
  Comparator #(.width(3)) comparator_10 (.a(Instruction[14:12]), .b(3'b001), .eq(comparator_10_eq));  // open: gt, lt
  Comparator #(.width(1)) comparator_11 (.a(Instruction[30]), .b(1'b0), .eq(comparator_11_eq));  // open: gt, lt
  Comparator #(.width(5)) comparator_12 (.a(Instruction[6:2]), .b(5'b00100), .eq(comparator_12_eq));  // open: gt, lt
  Comparator #(.width(3)) comparator_13 (.a(Instruction[14:12]), .b(3'b101), .eq(comparator_13_eq));  // open: gt, lt
  Comparator #(.width(1)) comparator_14 (.a(Instruction[30]), .b(1'b0), .eq(comparator_14_eq));  // open: gt, lt
  Comparator #(.width(5)) comparator_15 (.a(Instruction[6:2]), .b(5'b00100), .eq(comparator_15_eq));  // open: gt, lt
  Comparator #(.width(3)) comparator_16 (.a(Instruction[14:12]), .b(3'b101), .eq(comparator_16_eq));  // open: gt, lt
  Comparator #(.width(1)) comparator_17 (.a(Instruction[30]), .b(1'b1), .eq(comparator_17_eq));  // open: gt, lt
  Comparator #(.width(5)) comparator_18 (.a(Instruction[6:2]), .b(5'b00100), .eq(comparator_18_eq));  // open: gt, lt
  Comparator #(.width(3)) comparator_19 (.a(Instruction[14:12]), .b(3'b010), .eq(comparator_19_eq));  // open: gt, lt
  and and_1 (is_addi, comparator_1_eq, comparator_2_eq);
  and and_2 (is_andi, comparator_3_eq, comparator_4_eq);
  and and_3 (is_ori, comparator_5_eq, comparator_6_eq);
  and and_4 (is_xori, comparator_7_eq, comparator_8_eq);
  and and_5 (is_slli, comparator_9_eq, comparator_10_eq, comparator_11_eq);
  and and_6 (is_srli, comparator_12_eq, comparator_13_eq, comparator_14_eq);
  and and_7 (is_srai, comparator_15_eq, comparator_16_eq, comparator_17_eq);
  and and_8 (is_slti, comparator_18_eq, comparator_19_eq);
  ROM #(.addrWidth(6), .dataWidth(16)) rom_1 (.addr(input_ROM), .data(rom_1_data));
  Priority_Encoder #(.select_enc(6)) priority_encoder_1 (
    .in0(is_addi), .in1(is_andi), .in2(is_ori), .in3(is_xori), .in4(is_slli), .in5(is_srli), .in6(is_srai),
    .in7(is_slti), .out(input_ROM));  // open: in8, in9, in10, in11, in12, in13, in14, in15, in16, in17, in18, in19, in20, in21, in22, in23, in24, in25, in26, in27, in28, in29, in30, in31, in32, in33, in34, in35, in36, in37, in38, in39, in40, in41, in42, in43, in44, in45, in46, in47, in48, in49, in50, in51, in52, in53, in54, in55, in56, in57, in58, in59, in60, in61, in62, in63, gs, en_out, en_in

  // Other names for the same wires on the sheet: opcode[4:0] = Instruction[6:2]; funct3[2:0] = Instruction[14:12];
  //   funct7 = Instruction[30]

  // Notes on the sheet:
  //   INPUTS to your circuit
  //   Connect ROM Input here ->
  //   contents of rom_1 (hex, n*v repeats v):
  //   1041 13c1 1341 1241 10c1 12c1 16c1 1141
  //   ROM FOR CONTROL LOGIC
  //   DON'T CHANGE THE LOCATIONS OF THE INPUTS AND OUTPUTS!
  //   This is only if you choose to do the ROM option
  //   CONNECT
  //   WIRE
  //   TO
  //   USE
  //   ROM
  //   OUTPUT from your circuit
  //   Reminder: If using ROM, use combinational logic for PCSel
endmodule
